// Logisim project DataPath.circ as structural Verilog
module ALU (
  input  [31:0] A,
  input  [31:0] B,
  input  [3:0] SEL,
  output [31:0] Output,
  output Z_Flag,
  output N_Flagt,
  output [31:0] Hi_Lo
);

  wire comparator_1_lt, comparator_2_lt;
  wire [31:0] adder_1_out, and_1_out, bit_extender_1_out, bit_extender_2_out, divider_1_out, Hi,
       multiplier_1_out, nor_1_out, not_1_out, or_1_out, Rest, subtractor_1_out, xor_1_out;

  Multiplier #(.width(32)) multiplier_1 (.a(B), .b(A), .out(multiplier_1_out), .cout(Hi));  // open: cin
  Divider #(.width(32)) divider_1 (.a(A), .b(B), .out(divider_1_out), .rem(Rest));  // open: upper
  Adder #(.width(32)) adder_1 (.a(A), .b(B), .out(adder_1_out));  // open: cin, cout
  Subtractor #(.width(32)) subtractor_1 (.a(A), .b(B), .out(subtractor_1_out));  // open: bin, bout
  assign and_1_out = A & B;  // AND_Gate and_1, 32 bits wide
  assign or_1_out = A | B;  // OR_Gate or_1, 32 bits wide
  assign nor_1_out = ~(A | B);  // NOR_Gate nor_1, 32 bits wide
  assign xor_1_out = A ^ B;  // XOR_Gate xor_1, 32 bits wide
  assign not_1_out = ~A;  // NOT_Gate not_1, 32 bits wide
  Comparator #(.width(32), .mode("unsigned")) comparator_1 (.a(A), .b(B), .lt(comparator_1_lt));  // open: gt, eq
  Comparator #(.width(32)) comparator_2 (.a(B), .b(A), .lt(comparator_2_lt));  // open: gt, eq
  assign bit_extender_1_out = {{31{1'b0}}, comparator_1_lt};  // Bit_Extender bit_extender_1
  assign bit_extender_2_out = {{31{1'b0}}, comparator_2_lt};  // Bit_Extender bit_extender_2
  Multiplexer #(.select(4), .width(32), .enable("false")) multiplexer_1 (
    .in0(multiplier_1_out), .in1(divider_1_out), .in2(adder_1_out), .in3(subtractor_1_out), .in4(and_1_out),
    .in5(or_1_out), .in6(nor_1_out), .in7(xor_1_out), .in8(not_1_out), .in9(bit_extender_1_out),
    .in10(bit_extender_2_out), .out(Output), .sel(SEL));  // open: in11, in12, in13, in14, in15
  Multiplexer #(.width(32)) multiplexer_2 (.in0(Hi), .in1(Rest), .out(Hi_Lo), .sel(SEL[0]));  // open: en
  Comparator #(.width(32)) comparator_3 (.a(Output), .b({32{1'b0}}), .eq(Z_Flag), .lt(N_Flagt));  // open: gt

  // Other names for the same wires on the sheet: Selector[3:0] = SEL

  // Notes on the sheet:
  //   ARITHMETIC LOGIC UNIT(ALU)
endmodule

module Register_File (
  input  [31:0] DI,
  input  [4:0] DA,
  input  R_W,
  input  [4:0] SA,
  input  rst,
  input  CLOCK,
  input  [4:0] SB,
  output [31:0] A,
  output [31:0] B
);

  wire a0, a1, a2, a3, a4, a5, a6, a7, a8, a9, a10, a11, a12, a13, a14, a15, a16, a17, a18, a19, a20, a21,
       a22, a23, a24, a25, a26, a27, a28, a29, a30, a31;
  wire [31:0] q0, q1, q2, q3, q4, q5, q6, q7, q8, q9, q10, q11, q12, q13, q14, q15, q16, q17, q18, q19, q20,
       q21, q22, q23, q24, q25, q26, q27, q28, q29, q30, q31;

  Decoder #(.select(5), .disabled(0)) decoder_1 (
    .out0(a0), .out1(a1), .out2(a2), .out3(a3), .out4(a4), .out5(a5), .out6(a6), .out7(a7), .out8(a8),
    .out9(a9), .out10(a10), .out11(a11), .out12(a12), .out13(a13), .out14(a14), .out15(a15), .out16(a31),
    .out17(a30), .out18(a29), .out19(a28), .out20(a27), .out21(a26), .out22(a25), .out23(a24), .out24(a23),
    .out25(a22), .out26(a21), .out27(a20), .out28(a19), .out29(a18), .out30(a17), .out31(a16), .sel(DA),
    .en(R_W));
  Register #(.width(32)) Hi ();  // open: D, en, Q, clk, clr
  Register #(.width(32)) R0 (.D(DI), .en(a0), .Q(q0), .clk(CLOCK), .clr(rst));
  Register #(.width(32)) R4 (.D(DI), .en(a4), .Q(q4), .clk(CLOCK), .clr(rst));
  Register #(.width(32)) R8 (.D(DI), .en(a8), .Q(q8), .clk(CLOCK), .clr(rst));
  Register #(.width(32)) R12 (.D(DI), .en(a12), .Q(q12), .clk(CLOCK), .clr(rst));
  Register #(.width(32)) R16 (.D(DI), .en(a16), .Q(q16), .clk(CLOCK), .clr(rst));
  Register #(.width(32)) R20 (.D(DI), .en(a20), .Q(q20), .clk(CLOCK), .clr(rst));
  Register #(.width(32)) R24 (.D(DI), .en(a24), .Q(q24), .clk(CLOCK), .clr(rst));
  Register #(.width(32)) R28 (.D(DI), .en(a28), .Q(q28), .clk(CLOCK), .clr(rst));
  Register #(.width(32)) R1 (.D(DI), .en(a1), .Q(q1), .clk(CLOCK), .clr(rst));
  Register #(.width(32)) R5 (.D(DI), .en(a5), .Q(q5), .clk(CLOCK), .clr(rst));
  Register #(.width(32)) R9 (.D(DI), .en(a9), .Q(q9), .clk(CLOCK), .clr(rst));
  Register #(.width(32)) R13 (.D(DI), .en(a13), .Q(q13), .clk(CLOCK), .clr(rst));
  Register #(.width(32)) R17 (.D(DI), .en(a17), .Q(q17), .clk(CLOCK), .clr(rst));
  Register #(.width(32)) R21 (.D(DI), .en(a21), .Q(q21), .clk(CLOCK), .clr(rst));
  Register #(.width(32)) R25 (.D(DI), .en(a25), .Q(q25), .clk(CLOCK), .clr(rst));
  Register #(.width(32)) R29 (.D(DI), .en(a29), .Q(q29), .clk(CLOCK), .clr(rst));
  Register #(.width(32)) R2 (.D(DI), .en(a2), .Q(q2), .clk(CLOCK), .clr(rst));
  Register #(.width(32)) R6 (.D(DI), .en(a6), .Q(q6), .clk(CLOCK), .clr(rst));
  Register #(.width(32)) R10 (.D(DI), .en(a10), .Q(q10), .clk(CLOCK), .clr(rst));
  Register #(.width(32)) R14 (.D(DI), .en(a14), .Q(q14), .clk(CLOCK), .clr(rst));
  Register #(.width(32)) R18 (.D(DI), .en(a18), .Q(q18), .clk(CLOCK), .clr(rst));
  Register #(.width(32)) R22 (.D(DI), .en(a22), .Q(q22), .clk(CLOCK), .clr(rst));
  Register #(.width(32)) R26 (.D(DI), .en(a26), .Q(q26), .clk(CLOCK), .clr(rst));
  Register #(.width(32)) R30 (.D(DI), .en(a30), .Q(q30), .clk(CLOCK), .clr(rst));
  Register #(.width(32)) R3 (.D(DI), .en(a3), .Q(q3), .clk(CLOCK), .clr(rst));
  Register #(.width(32)) R7 (.D(DI), .en(a7), .Q(q7), .clk(CLOCK), .clr(rst));
  Register #(.width(32)) R11 (.D(DI), .en(a11), .Q(q11), .clk(CLOCK), .clr(rst));
  Register #(.width(32)) R15 (.D(DI), .en(a15), .Q(q15), .clk(CLOCK), .clr(rst));
  Register #(.width(32)) R19 (.D(DI), .en(a19), .Q(q19), .clk(CLOCK), .clr(rst));
  Register #(.width(32)) R23 (.D(DI), .en(a23), .Q(q23), .clk(CLOCK), .clr(rst));
  Register #(.width(32)) R27 (.D(DI), .en(a27), .Q(q27), .clk(CLOCK), .clr(rst));
  Register #(.width(32)) R31 (.D(DI), .en(a31), .Q(q31), .clk(CLOCK), .clr(rst));
  Multiplexer #(.select(5), .width(32)) multiplexer_1 (
    .in0(q0), .in1(q1), .in2(q2), .in3(q3), .in4(q4), .in5(q5), .in6(q6), .in7(q7), .in8(q8), .in9(q9),
    .in10(q10), .in11(q11), .in12(q12), .in13(q13), .in14(q14), .in15(q15), .in16(q16), .in17(q17),
    .in18(q18), .in19(q19), .in20(q20), .in21(q21), .in22(q22), .in23(q23), .in24(q24), .in25(q25),
    .in26(q26), .in27(q27), .in28(q28), .in29(q29), .in30(q30), .in31(q31), .out(A), .sel(SA));  // open: en
  Multiplexer #(.select(5), .width(32)) multiplexer_2 (
    .in0(q0), .in1(q1), .in2(q2), .in3(q3), .in4(q4), .in5(q5), .in6(q6), .in7(q7), .in8(q8), .in9(q9),
    .in10(q10), .in11(q11), .in12(q12), .in13(q13), .in14(q14), .in15(q15), .in16(q16), .in17(q17),
    .in18(q18), .in19(q19), .in20(q20), .in21(q21), .in22(q22), .in23(q23), .in24(q24), .in25(q25),
    .in26(q26), .in27(q27), .in28(q28), .in29(q29), .in30(q30), .in31(q31), .out(B), .sel(SB));  // open: en

  // Notes on the sheet:
  //   REGISTER FILE
endmodule

module Branch_Control (
  input  jump,
  input  FC,
  input  [31:0] IA,
  input  [31:0] k,
  output [31:0] IA_prime
);

  wire SEL;
  wire [31:0] multiplexer_1_out;

  and and_1 (SEL, jump, FC);
  Multiplexer #(.width(32), .enable("false")) multiplexer_1 (.in0(32'h4), .in1(k), .out(multiplexer_1_out), .sel(SEL));
  Adder #(.width(32)) adder_1 (.a(IA), .b(multiplexer_1_out), .out(IA_prime));  // open: cin, cout

  // Notes on the sheet:
  //   BRANCH CONTROL
endmodule

module Instruction_Decoder (
  input  [31:0] Inst,
  output [4:0] Rs,
  output [4:0] Rt,
  output [5:0] Op,
  output [15:0] k,
  output [27:0] Dest,
  output R_W,
  output [4:0] A,
  output I,
  output J,
  output R
);

  wire or_2_out;

  or or_1 (R_W, R, I);
  Multiplexer #(.width(5), .disabled(0), .enable("false")) multiplexer_1 (
    .in0(Inst[15:11]), .in1(Inst[20:16]), .out(A), .sel(I));
  Multiplexer #(.width(6), .disabled(0), .enable("false")) multiplexer_2 (
    .in0(Inst[5:0]), .in1(Inst[31:26]), .out(Op), .sel(or_2_out));
  or or_2 (or_2_out, I, J);
  Type_Decoder type_decoder_1 (.in_1(Inst[31:26]), .I(I), .J(J), .R(R));
  assign Dest = {{2{1'b0}}, Inst[25:0]};  // Bit_Extender bit_extender_1

  assign k = Inst[15:0];
  assign Rs = Inst[25:21];
  assign Rt = Inst[20:16];

  // Other names for the same wires on the sheet: D[25:0] = Inst[25:0]; func_code[5:0] = Inst[5:0];
  //   instruct[31:0] = Inst; Rd[4:0] = Inst[15:11]; op_code[5:0] = Inst[31:26]

  // Notes on the sheet:
  //   INSTRUCTION DECODER
endmodule

module Type_Decoder (
  input  [5:0] in_1,
  output I,
  output J,
  output R
);

  wire and_1_out, and_3_out, and_4_out, D___E___F___V___nD___nE___nF, nA___nB___nC, nD___nE___nF;

  nor nor_1 (nD___nE___nF, in_1[3], in_1[4], in_1[5]);
  and and_1 (and_1_out, in_1[3], in_1[4], in_1[5]);
  and and_2 (J, nA___nB___nC, ~in_1[3], in_1[4], ~in_1[5]);  // AND_Gate
  or or_1 (D___E___F___V___nD___nE___nF, nD___nE___nF, and_1_out);
  nor nor_2 (nA___nB___nC, in_1[0], in_1[1], in_1[2]);
  and and_3 (and_3_out, nA___nB___nC, nD___nE___nF);
  and and_4 (and_4_out, in_1[0], in_1[1], in_1[2], D___E___F___V___nD___nE___nF);
  or or_2 (R, and_3_out, and_4_out);
  nor nor_3 (I, J, R);

  // Other names for the same wires on the sheet: A = in_1[0]; B = in_1[1]; C = in_1[2]; D = in_1[3]; E = in_1[4];
  //   F = in_1[5]

  // Notes on the sheet:
  //   TYPE DECODER
endmodule

module Multiplicador_Con_Signo (
  input  [31:0] A,
  input  [31:0] B,
  output [31:0] out_3,
  output [31:0] out_4
);

  wire [30:0] Com_a2_A, Com_a2_B, multiplexer_1_out, multiplexer_2_out;

  Negator #(.width(31)) negator_1 (.in(A[30:0]), .out(Com_a2_A));
  Negator #(.width(31)) negator_2 (.in(B[30:0]), .out(Com_a2_B));
  xor xor_1 (out_4[31], B[31], A[31]);
  Multiplexer #(.width(31), .enable("false")) multiplexer_1 (
    .in0(A[30:0]), .in1(Com_a2_A), .out(multiplexer_1_out), .sel(A[31]));
  Multiplexer #(.width(31), .enable("false")) multiplexer_2 (
    .in0(B[30:0]), .in1(Com_a2_B), .out(multiplexer_2_out), .sel(B[31]));
  Multiplier #(.width(31)) multiplier_1 (
    .a(multiplexer_1_out), .b(multiplexer_2_out), .out(out_3[30:0]), .cout({out_4[29:0], out_3[31]}));  // open: cin

  assign out_4[30] = 1'b0;

  // Other names for the same wires on the sheet: A_t[30:0] = A[30:0]; Sign_A = A[31]; B_t[30:0] = B[30:0];
  //   Sign_B = B[31]; Mult[30:0] = out_3[30:0]; Hi_Mult[30:0] = {out_4[29:0], out_3[31]}; Sign = out_4[31]

  // Notes on the sheet:
  //   Multiplicador Con Signo
endmodule

module Divisor_con_Signo (
  input  [31:0] A,
  input  [31:0] B,
  output [31:0] out_3,
  output [31:0] out_4
);

  wire [30:0] Com_a2_A, Com_a2_B, multiplexer_1_out, multiplexer_2_out;

  Negator #(.width(31)) negator_1 (.in(A[30:0]), .out(Com_a2_A));
  Negator #(.width(31)) negator_2 (.in(B[30:0]), .out(Com_a2_B));
  xor xor_1 (out_4[31], B[31], A[31]);
  Multiplexer #(.width(31), .enable("false")) multiplexer_1 (
    .in0(A[30:0]), .in1(Com_a2_A), .out(multiplexer_1_out), .sel(A[31]));
  Multiplexer #(.width(31), .enable("false")) multiplexer_2 (
    .in0(B[30:0]), .in1(Com_a2_B), .out(multiplexer_2_out), .sel(B[31]));
  Multiplier #(.width(31)) multiplier_1 (
    .a(multiplexer_1_out), .b(multiplexer_2_out), .out(out_3[30:0]), .cout({out_4[29:0], out_3[31]}));  // open: cin

  assign out_4[30] = 1'b0;

  // Other names for the same wires on the sheet: A_t[30:0] = A[30:0]; Sign_A = A[31]; B_t[30:0] = B[30:0];
  //   Sign_B = B[31]; Mult[30:0] = out_3[30:0]; Hi_Mult[30:0] = {out_4[29:0], out_3[31]}; Sign = out_4[31]
endmodule
